# Fritzing sketch sensor_module_nrf24L01 (saved by Fritzing 0.9.3b)
breadboards: 1

parts:
  Part1 = Arduino Uno (Rev3)
  Part2 = NRF24L01

nets:
  N1: Part1.D9_PWM, Part2.CE
  N2: Part1.D10_PWM/SS, Part2.CSN
  N3: Part1.D11_PWM/MOSI, Part2.MOSI
  N4: Part1.D12/MISO, Part2.MISO
  N5: Part1.D13/SCK, Part2.SCK
  N6: Part1.D2, Part2.IRQ
  3V3: Part1.3V3, Part2.VCC
  GND: Part1.GND, Part2.GND
