# Fritzing sketch raspberrypi_gateway_nrf24L01 (saved by Fritzing 0.9.3b)

parts:
  Raspberry_Pi_1 = Raspberry Pi 3 [part_number=RPI-3-V1.2]
  Part1 = NRF24L01

nets:
  3V3: Raspberry_Pi_1.3v3, Part1.VCC
  N1: Raspberry_Pi_1.GIPO22, Part1.CE
  N2: Raspberry_Pi_1.GIPO10, Part1.MOSI
  N3: Raspberry_Pi_1.GIPO9, Part1.MISO
  N4: Raspberry_Pi_1.GIPO11, Part1.SCK
  N5: Raspberry_Pi_1.GIPO8, Part1.CSN
  GND: Raspberry_Pi_1.GND, Part1.GND
